# Fritzing sketch LORA_END_DEVICE_41x35 (saved by Fritzing 0.9.3b)
circuit board: 4.1cm x 3.5cm
breadboards: 1

parts:
  J6 = female pin header, 14 pins [form="♀ (female rounded)"]
  J7 = female pin header, 14 pins [form="♀ (female rounded)"]
  U4 = atmega168 [package=dip]
  RFM1 = RFM69HCW ISM Transciever
  J8 = female pin header, 3 pins [form="♀ (female)"]

nets:
  N1: J6.pin1, U4.RESET
  N2: J6.pin2, U4.D0_(RX)
  N3: J6.pin3, U4.D1_(TX)
  N4: J6.pin4, U4.D2, RFM1.14_DIO0
  N5: J6.pin5, U4.D3_(PWM)
  N6: J6.pin6, U4.D4
  N7: J6.pin7, J7.pin8, J7.pin9, U4.VCC, U4.AVCC, U4.AREF, RFM1.13_3.3V, J8.pin3
  N8: J6.pin8, U4.GND#7
  N9: J6.pin9, U4.XLAT1
  N10: J6.pin10, U4.XLAT2
  N11: J6.pin11, U4.D5_(PWM)
  N12: J6.pin12, U4.D6_(PWM)
  N13: J6.pin13, U4.D7
  N14: J6.pin14, U4.D8, RFM1.15_DIO1
  N15: J7.pin1, U4.A5
  N16: J7.pin2, U4.A4
  N17: J7.pin3, U4.A3
  N18: J7.pin4, U4.A2
  N19: J7.pin5, U4.A1
  N20: J7.pin6, U4.A0
  N21: J7.pin7, U4.GND#21, RFM1.1_GND, RFM1.10_GND, J8.pin2
  N22: J7.pin10, U4.D13, RFM1.4_SCK
  N23: J7.pin11, U4.D12, RFM1.2_MISO
  N24: J7.pin12, U4.D11_(PWM), RFM1.3_MOSI
  N25: J7.pin13, U4.D10_(PWM), RFM1.5_NSS_(CS)
  N26: J7.pin14, U4.D9_(PWM), RFM1.6_RESET
  N27: RFM1.9_ANT, J8.pin1

notes:
  This is a breadboard Arduino without an FTDI chip. You can program the chip with a USB-Serial breakout board, by using an external programmer or by programming the MCU in an Arduino board and then popping it into this circuit. The power source should be at least 7 VDC. Related example: http://itp.nyu.edu/physcomp/Tutorials/ArduinoBreadboard

custom parts:
  RFM69HCW ISM Transciever: RF Transceiver by Hope RF. Well supported Arduino libraries are available. This ISM band transceiver is available in several frequencies e.g. 433MHz and 915MHz and it is also available in various feature versions.
